# Fritzing sketch livella (saved by Fritzing 0.9.3b)
breadboards: 1

parts:
  LCD1 = LCD screen
  R1 = Rotary Potentiometer (Small) [maximum_resistance=100kΩ package=THT]
  hc-sr1 = hc-sr04
  hc-sr2 = hc-sr04
  hc-sr3 = hc-sr04
  Componente1 = Arduino Uno (Rev3)
  J1 = Buzzer
  R2 = Resistor [tolerance=±5% resistance=220 package="0603 [SMD]"]

nets:
  GND: LCD1.VSS, LCD1.R/W, LCD1.LED-, R1.leg1, hc-sr1.GND, hc-sr2.GND, hc-sr3.GND, Componente1.GND, J1.pin1
  VCC: LCD1.VDD, R1.leg2, hc-sr1.VCC, hc-sr2.VCC, hc-sr3.VCC, Componente1.5V, R2.Pin_0
  N1: LCD1.V0, R1.wiper
  N2: LCD1.RS, Componente1.A5/SCL
  N3: LCD1.E, Componente1.A4/SDA
  N4: LCD1.DB4, Componente1.A3
  N5: LCD1.DB5, Componente1.A2
  N6: LCD1.DB6, Componente1.A1
  N7: LCD1.DB7, Componente1.A0
  N8: LCD1.LED+, R2.Pin_1
  N9: hc-sr1.Trig, Componente1.D13/SCK
  N10: hc-sr1.Echo, Componente1.D12/MISO
  N11: hc-sr2.Trig, Componente1.D9_PWM
  N12: hc-sr2.Echo, Componente1.D8
  N13: hc-sr3.Trig, Componente1.D11_PWM/MOSI
  N14: hc-sr3.Echo, Componente1.D10_PWM/SS
  N15: Componente1.D5_PWM, J1.pin2

custom parts:
  Buzzer: Fixed frequency buzzer
