# Fritzing sketch schema (saved by Fritzing 0.9.3b)
breadboards: 1

parts:
  R1 = Resistor [tolerance=±5% resistance=220 package=THT]
  Componente1 = Arduino Uno (Rev3) - ICSP
  J1 = Buzzer
  LCD1 = LCD screen
  hc-sr1 = hc-sr04
  hc-sr2 = hc-sr04
  hc-sr3 = hc-sr04
  R2 = Rotary Potentiometer (Small) [maximum_resistance=100kΩ package=THT]

nets:
  VCC: R1.Pin_0, Componente1.5V, LCD1.VDD, hc-sr1.VCC, hc-sr2.VCC, hc-sr3.VCC, R2.leg2
  N1: R1.Pin_1, LCD1.LED+
  N2: Componente1.A0, J1.pin2
  N3: Componente1.D8, hc-sr3.Echo
  N4: Componente1.D9_PWM, hc-sr3.Trig
  N5: Componente1.D10_PWM/SS, hc-sr2.Echo
  N6: Componente1.D11_PWM/MOSI, hc-sr2.Trig
  N7: Componente1.D12/MISO, hc-sr1.Echo
  N8: Componente1.D13/SCK, hc-sr1.Trig
  N9: Componente1.D2, LCD1.DB7
  N10: Componente1.D3_PWM, LCD1.DB6
  N11: Componente1.D4, LCD1.DB5
  N12: Componente1.D5_PWM, LCD1.DB4
  N13: Componente1.D6_PWM, LCD1.RS
  N14: Componente1.D7, LCD1.E
  GND: Componente1.GND, J1.pin1, LCD1.VSS, LCD1.R/W, LCD1.LED-, hc-sr1.GND, hc-sr2.GND, hc-sr3.GND, R2.leg1
  N15: LCD1.V0, R2.wiper

custom parts:
  Buzzer: Fixed frequency buzzer
